# Fritzing sketch gas-leakage-alarm (saved by Fritzing 1.0.0d)

parts:
  WeMos_D1_Mini1 = WeMos D1 Mini
  J1 = Piezo Speaker
  Mod1 = MQ-7 breakout
  LED1 = smd LED [color="Green (570nm)" package="0805 [SMD]"]
  LED2 = smd LED [color="Yellow (595nm)" package="0805 [SMD]"]
  LED3 = smd LED [color="Yellow (595nm)" package="0805 [SMD]"]
  LED4 = smd LED [color="Red (633nm)" package="0805 [SMD]"]
  LED5 = smd LED [color="Blue (525nm)" package="0805 [SMD]"]
  R1 = Resistor [tolerance=±5% resistance=470 power=0.25W package="0402 [SMD]"]
  R2 = Resistor [tolerance=±5% resistance=2.2k power=0.25W package="0402 [SMD]"]
  R3 = Resistor [tolerance=±5% resistance=2.2k power=0.25W package="0402 [SMD]"]
  R4 = Resistor [tolerance=±5% resistance=2.2k power=0.25W package="0402 [SMD]"]
  R5 = Resistor [tolerance=±5% resistance=2.2k power=0.25W package="0402 [SMD]"]

nets:
  5V: WeMos_D1_Mini1.5V, Mod1.VCC
  N1: WeMos_D1_Mini1.A0, Mod1.AO
  N2: WeMos_D1_Mini1.D1, R1.Pin_0
  N3: WeMos_D1_Mini1.D2, R2.Pin_0
  N4: WeMos_D1_Mini1.D5, R3.Pin_1
  N5: WeMos_D1_Mini1.D6, R4.Pin_1
  N6: WeMos_D1_Mini1.D7, R5.Pin_1
  N7: WeMos_D1_Mini1.D8, J1.pin2
  N8: WeMos_D1_Mini1.G, J1.pin1, Mod1.GND, LED1.cathode, LED2.cathode, LED3.cathode, LED4.cathode, LED5.cathode
  N9: LED1.anode, R1.Pin_1
  N10: LED2.anode, R2.Pin_1
  N11: LED3.anode, R3.Pin_0
  N12: LED4.anode, R4.Pin_0
  N13: LED5.anode, R5.Pin_0

custom parts:
  MQ-7 breakout: MQ-5 gas sensor
